# Fritzing sketch schematic (saved by Fritzing 0.9.3b)
breadboards: 1

parts:
  Componente1 = Arduino Mega 2560 (Rev3)
  hc-sr1 = hc-sr04

nets:
  5V: Componente1.5V, hc-sr1.VCC
  GND: Componente1.GND, hc-sr1.GND
  N1: Componente1.D2_PWM, hc-sr1.Trig
  N2: Componente1.D3_PWM, hc-sr1.Echo
